# Fritzing sketch 2023-0612-car-1 (saved by Fritzing 0.8.7b)
breadboards: 1

parts:
  부품1 = Arduino Uno (Rev3)
  S1 = H-Bridge with L298N
  M1 = DC Motor
  J1 = Basic Servo

nets:
  N1: 부품1.D9_PWM, J1.pulse
  N2: 부품1.D11_PWM/MOSI, S1.ENA
  N3: 부품1.D2, S1.IN1
  N4: 부품1.D3_PWM, S1.IN2
  5V: 부품1.5V, S1.5V, J1.vcc
  GND: 부품1.GND, S1.GND, J1.gnd
  VIN: 부품1.VIN, S1.12V
  N5: S1.M1-01, M1.pin_2
  N6: S1.M1-02, M1.pin_1

custom parts:
  H-Bridge with L298N: h-bridge
