# Fritzing sketch Flitzing_410 (saved by Fritzing 0.8.7b)
breadboards: 1

parts:
  LED1 = RGB LED (com. anode, rbg) [package="5 mm [THT]"]
  R1 = Resistor [tolerance=±5% resistance=220 package=THT]

nets:
  N1: LED1.common_anode, R1.Pin_1
