# Fritzing sketch Flitzing_410_2 (saved by Fritzing 0.8.7b)
breadboards: 1

parts:
  Mod1 = KY-015 Temperature & Humidity Sensor Module [package="Breakout board"]
  부품1 = Arduino Uno (Rev3)

nets:
  N1: Mod1.S, 부품1.D2
  VIN: Mod1.Vin, 부품1.5V
  N2: Mod1.-, 부품1.GND

custom parts:
  KY-015 Temperature & Humidity Sensor Module: KY-015 temperature and humidity sensor module, provides a low-latency serial interface to measure humidity and temperature.
