# Fritzing sketch Untitled Sketch 3 moter (saved by Fritzing 0.8.7b)
breadboards: 1

parts:
  S1 = H-Bridge with L298N
  부품1 = Arduino Uno (Rev3)
  M1 = DC Motor
  J1 = Basic Servo
  VCC1 = Battery block 9V  # not connected

nets:
  12V: S1.12V, 부품1.VIN
  GND: S1.GND, 부품1.GND, J1.gnd
  5V: S1.5V, 부품1.5V, J1.vcc
  N1: S1.ENA, 부품1.D11_PWM/MOSI
  N2: S1.IN1, 부품1.D2
  N3: S1.IN2, 부품1.D3_PWM
  N4: S1.M1-01, M1.pin_2
  N5: S1.M1-02, M1.pin_1
  N6: 부품1.D9_PWM, J1.pulse

custom parts:
  H-Bridge with L298N: h-bridge
